// Logisim project hw4.circ as structural Verilog: 14 circuits, main circuit main
module main (
  input  reset
);

  wire and_1_out, and_2_out, clock, keyboard_1_avail, m1, m2, m3, m4, m5, m6, m7, m8, m9, m10, m11,
       not_1_out, not_3_out, or_1_out, zeroCheck;
  wire [2:0] aluCntrl, L3, multiplexer_2_out, multiplexer_3_out, multiplexer_5_out, Rd, Rs, Rt;
  wire [3:0] OPCode;
  wire [6:0] keyboard_1_data;
  wire [7:0] inpval;
  wire [15:0] _6bitIm, adder_2_result, ALUout, multiplexer_1_out, multiplexer_4_out, multiplexer_6_out,
       multiplexer_7_out, multiplexer_8_out, multiplexer_10_out, n12_16ext_1_out_2, PCin, PCjal, PCout,
       ram_1_data, RS1, RS2;

  PC pc_1 (.Res(reset), .clock(clock), .\input (PCin), .\output (PCout));
  Clock clock_1 (.out(clock));
  ADDER adder_1 (.B(16'h1), .sub(1'b0), .A(PCout), .result(PCjal));  // open: ovf
  ROM #(.addrWidth(16), .dataWidth(16)) rom_1 (.addr(PCout), .data({OPCode, Rs, Rt, Rd, L3}));  // open: sel
  Multiplexer #(.width(16), .enable("false")) multiplexer_1 (
    .in0(multiplexer_4_out), .in1(PCjal), .out(multiplexer_1_out), .sel(m5));
  Multiplexer #(.width(3), .enable("false")) multiplexer_2 (
    .in0(multiplexer_3_out), .in1(3'b111), .out(multiplexer_2_out), .sel(m5));
  Multiplexer #(.width(3), .enable("false")) multiplexer_3 (.in0(Rd), .in1(Rt), .out(multiplexer_3_out), .sel(m6));
  not not_1 (not_1_out, clock);
  ADDER adder_2 (.B(_6bitIm), .sub(1'b0), .A(PCjal), .result(adder_2_result));  // open: ovf
  or or_1 (or_1_out, and_1_out, and_2_out);
  and and_1 (and_1_out, m8, zeroCheck);
  and and_2 (and_2_out, m9, ALUout[15]);
  Multiplexer #(.width(16), .enable("false")) multiplexer_4 (
    .in0(multiplexer_10_out), .in1({{8{1'b0}}, inpval}), .out(multiplexer_4_out), .sel(m10));
  RegisterFile registerfile_1 (
    .RDVAL(multiplexer_1_out), .RD(multiplexer_2_out), .RS2VAL(RS2), .RS1VAL(RS1), .Clock_pin(not_1_out),
    .res(reset), .WE(m1), .RS1(multiplexer_5_out), .RS2(Rs));
  Multiplexer #(.width(3), .enable("false")) multiplexer_5 (.in0(Rt), .in1(3'b111), .out(multiplexer_5_out), .sel(m7));
  Multiplexer #(.width(16), .enable("false")) multiplexer_6 (
    .in0(PCjal), .in1(adder_2_result), .out(multiplexer_6_out), .sel(or_1_out));
  TTY #(.rows(13), .cols(80), .trigger("falling")) tty_1 (.data(RS2[6:0]), .clk(clock), .we(m11), .clr(reset));
  _12_16ext u_12_16ext_1 (.in_1({Rs, Rt, Rd, L3}), .out_2(n12_16ext_1_out_2));
  Multiplexer #(.width(16), .enable("false")) multiplexer_7 (
    .in0(RS1), .in1(_6bitIm), .out(multiplexer_7_out), .sel(m2));
  Multiplexer #(.width(16), .enable("false")) multiplexer_8 (
    .in0(multiplexer_6_out), .in1(n12_16ext_1_out_2), .out(multiplexer_8_out), .sel(m5));
  ALU alu_1 (.B(multiplexer_7_out), .A(RS2), .zero(zeroCheck), .\output (ALUout), .shamt(L3), .controlOpCode(aluCntrl));
  Multiplexer #(.width(16), .enable("false")) multiplexer_9 (.in0(multiplexer_8_out), .in1(RS1), .out(PCin), .sel(m7));
  Keyboard #(.buflen(7)) keyboard_1 (
    .clk(clock), .re(m10), .clr(reset), .avail(keyboard_1_avail), .data(keyboard_1_data));
  Multiplexer #(.width(16), .enable("false")) multiplexer_10 (
    .in0(ALUout), .in1(ram_1_data), .out(multiplexer_10_out), .sel(m4));
  not not_2 (inpval[7], keyboard_1_avail);
  not not_3 (not_3_out, clock);
  Multiplexer #(.width(7), .enable("false")) multiplexer_11 (
    .in0(keyboard_1_data), .in1({7{1'b0}}), .out(inpval[6:0]), .sel(inpval[7]));
  RAM #(.addrWidth(16), .dataWidth(16), .bus("separate")) ram_1 (
    .addr(ALUout), .din(RS1), .data(ram_1_data), .str(m3), .clk(not_3_out));  // open: sel, ld, clr
  _6_16ext u_6_16ext_1 (.in_1({Rd, L3}), .out_2(_6bitIm));
  CONTROL control_1 (
    .opcode(OPCode), .m10(m10), .m5(m5), .m11(m11), .m1(m1), .m6(m6), .m7(m7), .m2(m2), .m8(m8), .m3(m3),
    .m9(m9), .m4(m4), .alucntr(aluCntrl));

  // Other names for the same wires on the sheet: res = reset

  // Notes on the sheet:
  //   contents of rom_1 (hex, n*v repeats v):
  //   f000 f008 f010 f018 e000 e200 e400 e600
  //   General
  //   PC_Calc
  //   Output
  //   Input
endmodule

module CONTROL (
  input  [3:0] opcode,
  output m3,
  output m4,
  output m2,
  output m1,
  output m7,
  output m8,
  output m9,
  output m5,
  output m6,
  output m10,
  output m11,
  output [2:0] alucntr
);

  wire and_2_out, and_3_out, and_4_out, and_5_out, and_7_out, and_8_out, and_9_out, and_11_out, and_12_out,
       and_15_out, and_17_out, and_18_out, and_21_out, nand_1_out, nor_1_out, not_1_out, not_2_out,
       not_3_out, not_4_out, not_5_out, not_6_out, not_7_out, not_8_out, not_9_out, not_10_out, not_11_out,
       not_12_out, not_13_out, not_14_out, not_15_out, not_16_out, not_17_out, not_18_out, not_19_out,
       not_20_out, not_21_out, not_22_out, not_23_out, not_24_out, not_25_out, not_26_out, not_27_out,
       not_28_out, not_29_out, not_30_out, not_31_out, not_32_out, not_33_out, not_34_out, not_35_out,
       not_36_out, not_37_out, not_38_out, not_39_out, xnor_1_out, xor_1_out;

  not not_1 (not_1_out, opcode[1]);
  not not_2 (not_2_out, opcode[0]);
  and and_1 (m10, opcode[0], opcode[1], opcode[3]);
  not not_3 (not_3_out, opcode[3]);
  not not_4 (not_4_out, opcode[0]);
  not not_5 (not_5_out, opcode[2]);
  not not_6 (not_6_out, opcode[1]);
  and and_2 (and_2_out, not_4_out, not_6_out, not_5_out, not_3_out);
  and and_3 (and_3_out, not_2_out, not_1_out, opcode[2], opcode[3]);
  or or_1 (m5, and_3_out, and_5_out);
  not not_7 (not_7_out, opcode[0]);
  not not_8 (not_8_out, opcode[3]);
  and and_4 (and_4_out, not_8_out, opcode[2]);
  not not_9 (not_9_out, opcode[2]);
  and and_5 (and_5_out, opcode[0], opcode[1], not_9_out, opcode[3]);
  and and_6 (m11, not_7_out, opcode[1], opcode[2], opcode[3]);
  nand nand_1 (nand_1_out, opcode[0], opcode[1]);
  and and_7 (and_7_out, nand_1_out, not_11_out, opcode[3]);
  or or_2 (m1, and_2_out, and_4_out, and_7_out, and_12_out);
  not not_10 (not_10_out, opcode[0]);
  not not_11 (not_11_out, opcode[2]);
  not not_12 (not_12_out, opcode[2]);
  not not_13 (not_13_out, opcode[3]);
  and and_8 (and_8_out, not_12_out, not_15_out);
  and and_9 (and_9_out, not_10_out, opcode[1], opcode[2], not_13_out);
  or or_3 (m6, and_9_out, and_8_out);
  not not_14 (not_14_out, opcode[2]);
  xor xor_1 (xor_1_out, opcode[0], opcode[1]);
  and and_10 (alucntr[2], xor_1_out, not_14_out, opcode[3]);
  and and_11 (and_11_out, opcode[2], opcode[3]);
  xnor xnor_1 (xnor_1_out, opcode[0], opcode[1]);
  and and_12 (and_12_out, xnor_1_out, and_11_out);
  not not_15 (not_15_out, opcode[3]);
  not not_16 (not_16_out, opcode[1]);
  nor nor_1 (nor_1_out, opcode[1], opcode[2], opcode[3]);
  not not_17 (not_17_out, opcode[1]);
  and and_13 (m7, opcode[0], not_17_out, opcode[2], opcode[3]);
  not not_18 (not_18_out, opcode[3]);
  and and_14 (alucntr[1], not_16_out, opcode[2], not_18_out);
  not not_19 (not_19_out, opcode[0]);
  and and_15 (and_15_out, not_19_out, opcode[1], opcode[2], not_23_out);
  or or_4 (m2, nor_1_out, and_15_out);
  not not_20 (not_20_out, opcode[0]);
  and and_16 (m8, not_20_out, opcode[1], not_24_out, not_25_out);
  not not_21 (not_21_out, opcode[1]);
  not not_22 (not_22_out, opcode[3]);
  and and_17 (and_17_out, opcode[0], not_21_out, opcode[2], not_22_out);
  or or_5 (alucntr[0], and_17_out, and_18_out, and_21_out);
  not not_23 (not_23_out, opcode[3]);
  not not_24 (not_24_out, opcode[2]);
  not not_25 (not_25_out, opcode[3]);
  not not_26 (not_26_out, opcode[2]);
  not not_27 (not_27_out, opcode[1]);
  and and_18 (and_18_out, opcode[0], not_27_out, not_26_out, opcode[3]);
  not not_28 (not_28_out, opcode[1]);
  not not_29 (not_29_out, opcode[3]);
  not not_30 (not_30_out, opcode[2]);
  and and_19 (m3, opcode[0], not_28_out, not_30_out, not_29_out);
  not not_31 (not_31_out, opcode[3]);
  not not_32 (not_32_out, opcode[2]);
  and and_20 (m9, opcode[0], opcode[1], not_32_out, not_31_out);
  not not_33 (not_33_out, opcode[1]);
  not not_34 (not_34_out, opcode[2]);
  not not_35 (not_35_out, opcode[0]);
  and and_21 (and_21_out, not_35_out, not_33_out, not_34_out, opcode[3]);
  not not_36 (not_36_out, opcode[3]);
  not not_37 (not_37_out, opcode[0]);
  not not_38 (not_38_out, opcode[2]);
  not not_39 (not_39_out, opcode[1]);
  and and_22 (m4, not_37_out, not_39_out, not_38_out, not_36_out);

  // Other names for the same wires on the sheet: o0 = opcode[0]; o1 = opcode[1]; o2 = opcode[2]; _03 = opcode[3]

  // Notes on the sheet:
  //   input
  //   Jal or J
  //   output
  //   register write enable
  //   reg store adress
  //   aluControl-2
  //   aluControl-1
  //   jr
  //   immed for alu
  //   beq
  //   aluControl-0
  //   we for data
  //   blt
  //   load from data
endmodule

module RegisterFile (
  input  Clock_pin,
  input  res,
  input  [15:0] RDVAL,
  input  WE,
  input  [2:0] RD,
  input  [2:0] RS1,
  input  [2:0] RS2,
  output [15:0] RS2VAL,
  output [15:0] RS1VAL
);

  wire and_1_out, and_2_out, and_3_out, and_4_out, and_5_out, and_6_out, and_7_out, and_8_out, and_9_out,
       decoder_1_out0, decoder_1_out1, decoder_1_out2, decoder_1_out3, decoder_1_out4, decoder_1_out5,
       decoder_1_out6, decoder_1_out7;
  wire [15:0] _1, _2, _3, _4, _5, _6, _7, _8;

  // Probe on _1
  // Probe on _2
  Decoder #(.select(3), .enable("false")) decoder_1 (
    .out0(decoder_1_out0), .out1(decoder_1_out1), .out2(decoder_1_out2), .out3(decoder_1_out3),
    .out4(decoder_1_out4), .out5(decoder_1_out5), .out6(decoder_1_out6), .out7(decoder_1_out7), .sel(RD));
  // Probe on _3
  and and_1 (and_1_out, Clock_pin, WE);
  // Probe on _4
  // Probe on _5
  and and_2 (and_2_out, decoder_1_out0, and_1_out);
  and and_3 (and_3_out, decoder_1_out1, and_1_out);
  and and_4 (and_4_out, decoder_1_out2, and_1_out);
  and and_5 (and_5_out, decoder_1_out3, and_1_out);
  and and_6 (and_6_out, decoder_1_out4, and_1_out);
  and and_7 (and_7_out, decoder_1_out5, and_1_out);
  and and_8 (and_8_out, decoder_1_out6, and_1_out);
  and and_9 (and_9_out, decoder_1_out7, and_1_out);
  // Probe on _6
  _16bitregister u_16bitregister_1 (.Res(res), .WER(and_2_out), .\input (RDVAL), .\output (_1));
  _16bitregister u_16bitregister_2 (.Res(res), .WER(and_3_out), .\input (RDVAL), .\output (_2));
  _16bitregister u_16bitregister_3 (.Res(res), .WER(and_4_out), .\input (RDVAL), .\output (_3));
  _16bitregister u_16bitregister_4 (.Res(res), .WER(and_5_out), .\input (RDVAL), .\output (_4));
  _16bitregister u_16bitregister_5 (.Res(res), .WER(and_6_out), .\input (RDVAL), .\output (_5));
  _16bitregister u_16bitregister_6 (.Res(res), .WER(and_7_out), .\input (RDVAL), .\output (_6));
  _16bitregister u_16bitregister_7 (.Res(res), .WER(and_8_out), .\input (RDVAL), .\output (_7));
  _16bitregister u_16bitregister_8 (.Res(res), .WER(and_9_out), .\input (RDVAL), .\output (_8));
  // Probe on _7
  // Probe on _8
  Multiplexer #(.select(3), .width(16), .enable("false")) multiplexer_1 (
    .in0(_1), .in1(_2), .in2(_3), .in3(_4), .in4(_5), .in5(_6), .in6(_7), .in7(_8), .out(RS2VAL), .sel(RS2));
  Multiplexer #(.select(3), .width(16), .enable("false")) multiplexer_2 (
    .in0(_1), .in1(_2), .in2(_3), .in3(_4), .in4(_5), .in5(_6), .in6(_7), .in7(_8), .out(RS1VAL), .sel(RS1));
endmodule

module ALU (
  input  [15:0] A,
  input  [15:0] B,
  input  [2:0] controlOpCode,
  input  [2:0] shamt,
  output zero,
  output [15:0] \output 
);

  wire [15:0] Adderout, \not , sL, sR, \xor ;

  not not_1 (\not [0], A[0]);
  not not_2 (\not [1], A[1]);
  not not_3 (\not [2], A[2]);
  not not_4 (\not [3], A[3]);
  not not_5 (\not [4], A[4]);
  not not_6 (\not [5], A[5]);
  not not_7 (\not [6], A[6]);
  not not_8 (\not [7], A[7]);
  not not_9 (\not [8], A[8]);
  not not_10 (\not [9], A[9]);
  not not_11 (\not [10], A[10]);
  not not_12 (\not [11], A[11]);
  not not_13 (\not [12], A[12]);
  not not_14 (\not [13], A[13]);
  not not_15 (\not [14], A[14]);
  not not_16 (\not [15], A[15]);
  ADDER adder_1 (.B(B), .sub(controlOpCode[0]), .A(A), .result(Adderout));  // open: ovf
  _3BitShiftL u_3bitshiftl_1 (.in_1(A), .in_2(shamt), .out_3(sL));
  _3BitShiftR u_3bitshiftr_1 (.in_1(A), .in_2(shamt), .out_3(sR));
  nor nor_1 (zero, Adderout[0], Adderout[1], Adderout[2], Adderout[3], Adderout[4], Adderout[5], Adderout[6], Adderout[7], Adderout[8], Adderout[9], Adderout[10], Adderout[11], Adderout[12], Adderout[13], Adderout[14], Adderout[15]);
  xor xor_1 (\xor [0], A[0], B[0]);
  xor xor_2 (\xor [1], A[1], B[1]);
  xor xor_3 (\xor [2], A[2], B[2]);
  xor xor_4 (\xor [3], A[3], B[3]);
  xor xor_5 (\xor [4], A[4], B[4]);
  xor xor_6 (\xor [5], A[5], B[5]);
  xor xor_7 (\xor [6], A[6], B[6]);
  xor xor_8 (\xor [7], A[7], B[7]);
  xor xor_9 (\xor [8], A[8], B[8]);
  xor xor_10 (\xor [9], A[9], B[9]);
  xor xor_11 (\xor [10], A[10], B[10]);
  xor xor_12 (\xor [11], A[11], B[11]);
  xor xor_13 (\xor [12], A[12], B[12]);
  xor xor_14 (\xor [13], A[13], B[13]);
  xor xor_15 (\xor [14], A[14], B[14]);
  xor xor_16 (\xor [15], A[15], B[15]);
  Multiplexer #(.select(3), .width(16), .enable("false")) multiplexer_1 (
    .in0(Adderout), .in1(Adderout), .in2(\not ), .in3(\xor ), .in4(sL), .in5(sR), .out(\output ),
    .sel(controlOpCode));  // open: in6, in7

  // Other names for the same wires on the sheet: Ain[15:0] = A; Bin[15:0] = B; fullOp[2:0] = controlOpCode;
  //   op0 = controlOpCode[0]; shm[2:0] = shamt
endmodule

module PC (
  input  Res,
  input  clock,
  input  [15:0] \input ,
  output [15:0] \output 
);

  D_Flip_Flop d_ff_1 (.clk(clock), .D(\input [0]), .Q(\output [0]), .reset(Res));  // open: Qn, preset, en
  D_Flip_Flop d_ff_2 (.clk(clock), .D(\input [1]), .Q(\output [1]), .reset(Res));  // open: Qn, preset, en
  D_Flip_Flop d_ff_3 (.clk(clock), .D(\input [2]), .Q(\output [2]), .reset(Res));  // open: Qn, preset, en
  D_Flip_Flop d_ff_4 (.clk(clock), .D(\input [3]), .Q(\output [3]), .reset(Res));  // open: Qn, preset, en
  D_Flip_Flop d_ff_5 (.clk(clock), .D(\input [4]), .Q(\output [4]), .reset(Res));  // open: Qn, preset, en
  D_Flip_Flop d_ff_6 (.clk(clock), .D(\input [5]), .Q(\output [5]), .reset(Res));  // open: Qn, preset, en
  D_Flip_Flop d_ff_7 (.clk(clock), .D(\input [6]), .Q(\output [6]), .reset(Res));  // open: Qn, preset, en
  D_Flip_Flop d_ff_8 (.clk(clock), .D(\input [7]), .Q(\output [7]), .reset(Res));  // open: Qn, preset, en
  D_Flip_Flop d_ff_9 (.clk(clock), .D(\input [8]), .Q(\output [8]), .reset(Res));  // open: Qn, preset, en
  D_Flip_Flop d_ff_10 (.clk(clock), .D(\input [9]), .Q(\output [9]), .reset(Res));  // open: Qn, preset, en
  D_Flip_Flop d_ff_11 (.clk(clock), .D(\input [10]), .Q(\output [10]), .reset(Res));  // open: Qn, preset, en
  D_Flip_Flop d_ff_12 (.clk(clock), .D(\input [11]), .Q(\output [11]), .reset(Res));  // open: Qn, preset, en
  D_Flip_Flop d_ff_13 (.clk(clock), .D(\input [12]), .Q(\output [12]), .reset(Res));  // open: Qn, preset, en
  D_Flip_Flop d_ff_14 (.clk(clock), .D(\input [13]), .Q(\output [13]), .reset(Res));  // open: Qn, preset, en
  D_Flip_Flop d_ff_15 (.clk(clock), .D(\input [14]), .Q(\output [14]), .reset(Res));  // open: Qn, preset, en
  D_Flip_Flop d_ff_16 (.clk(clock), .D(\input [15]), .Q(\output [15]), .reset(Res));  // open: Qn, preset, en
endmodule

module _6_16ext (
  input  [5:0] in_1,
  output [15:0] out_2
);


  assign out_2 = {{11{in_1[5]}}, in_1[4:0]};
endmodule

module _12_16ext (
  input  [11:0] in_1,
  output [15:0] out_2
);


  assign out_2 = {4'b0000, in_1};
endmodule

module _16bitregister (
  input  Res,
  input  WER,
  input  [15:0] \input ,
  output [15:0] \output 
);

  D_Flip_Flop d_ff_1 (.clk(WER), .D(\input [0]), .Q(\output [0]), .reset(Res));  // open: Qn, preset, en
  D_Flip_Flop d_ff_2 (.clk(WER), .D(\input [1]), .Q(\output [1]), .reset(Res));  // open: Qn, preset, en
  D_Flip_Flop d_ff_3 (.clk(WER), .D(\input [2]), .Q(\output [2]), .reset(Res));  // open: Qn, preset, en
  D_Flip_Flop d_ff_4 (.clk(WER), .D(\input [3]), .Q(\output [3]), .reset(Res));  // open: Qn, preset, en
  D_Flip_Flop d_ff_5 (.clk(WER), .D(\input [4]), .Q(\output [4]), .reset(Res));  // open: Qn, preset, en
  D_Flip_Flop d_ff_6 (.clk(WER), .D(\input [5]), .Q(\output [5]), .reset(Res));  // open: Qn, preset, en
  D_Flip_Flop d_ff_7 (.clk(WER), .D(\input [6]), .Q(\output [6]), .reset(Res));  // open: Qn, preset, en
  D_Flip_Flop d_ff_8 (.clk(WER), .D(\input [7]), .Q(\output [7]), .reset(Res));  // open: Qn, preset, en
  D_Flip_Flop d_ff_9 (.clk(WER), .D(\input [8]), .Q(\output [8]), .reset(Res));  // open: Qn, preset, en
  D_Flip_Flop d_ff_10 (.clk(WER), .D(\input [9]), .Q(\output [9]), .reset(Res));  // open: Qn, preset, en
  D_Flip_Flop d_ff_11 (.clk(WER), .D(\input [10]), .Q(\output [10]), .reset(Res));  // open: Qn, preset, en
  D_Flip_Flop d_ff_12 (.clk(WER), .D(\input [11]), .Q(\output [11]), .reset(Res));  // open: Qn, preset, en
  D_Flip_Flop d_ff_13 (.clk(WER), .D(\input [12]), .Q(\output [12]), .reset(Res));  // open: Qn, preset, en
  D_Flip_Flop d_ff_14 (.clk(WER), .D(\input [13]), .Q(\output [13]), .reset(Res));  // open: Qn, preset, en
  D_Flip_Flop d_ff_15 (.clk(WER), .D(\input [14]), .Q(\output [14]), .reset(Res));  // open: Qn, preset, en
  D_Flip_Flop d_ff_16 (.clk(WER), .D(\input [15]), .Q(\output [15]), .reset(Res));  // open: Qn, preset, en
endmodule

module ADDER (
  input  [15:0] B,
  input  [15:0] A,
  input  sub,
  output [15:0] result,
  output ovf
);

  wire n1bitadd_1_carryout, n1bitadd_2_carryout, n1bitadd_3_carryout, n1bitadd_4_carryout,
       n1bitadd_5_carryout, n1bitadd_6_carryout, n1bitadd_7_carryout, n1bitadd_8_carryout,
       n1bitadd_9_carryout, n1bitadd_10_carryout, n1bitadd_11_carryout, n1bitadd_12_carryout,
       n1bitadd_13_carryout, n1bitadd_14_carryout, n1bitadd_15_carryout, n1bitadd_16_carryout, xor_1_out,
       xor_2_out, xor_3_out, xor_4_out, xor_5_out, xor_6_out, xor_7_out, xor_8_out, xor_9_out, xor_10_out,
       xor_11_out, xor_12_out, xor_13_out, xor_14_out, xor_15_out, xor_16_out;

  xor xor_1 (xor_1_out, B[0], sub);
  _1bitAdd u_1bitadd_1 (.b(xor_1_out), .a(A[0]), .carryin(sub), .carryout(n1bitadd_1_carryout), .out(result[0]));
  xor xor_2 (xor_2_out, B[1], sub);
  _1bitAdd u_1bitadd_2 (
    .b(xor_2_out), .a(A[1]), .carryin(n1bitadd_1_carryout), .carryout(n1bitadd_2_carryout), .out(result[1]));
  xor xor_3 (xor_3_out, B[2], sub);
  _1bitAdd u_1bitadd_3 (
    .b(xor_3_out), .a(A[2]), .carryin(n1bitadd_2_carryout), .carryout(n1bitadd_3_carryout), .out(result[2]));
  xor xor_4 (xor_4_out, B[3], sub);
  _1bitAdd u_1bitadd_4 (
    .b(xor_4_out), .a(A[3]), .carryin(n1bitadd_3_carryout), .carryout(n1bitadd_4_carryout), .out(result[3]));
  xor xor_5 (xor_5_out, B[4], sub);
  _1bitAdd u_1bitadd_5 (
    .b(xor_5_out), .a(A[4]), .carryin(n1bitadd_4_carryout), .carryout(n1bitadd_5_carryout), .out(result[4]));
  xor xor_6 (xor_6_out, B[5], sub);
  _1bitAdd u_1bitadd_6 (
    .b(xor_6_out), .a(A[5]), .carryin(n1bitadd_5_carryout), .carryout(n1bitadd_6_carryout), .out(result[5]));
  xor xor_7 (xor_7_out, B[6], sub);
  _1bitAdd u_1bitadd_7 (
    .b(xor_7_out), .a(A[6]), .carryin(n1bitadd_6_carryout), .carryout(n1bitadd_7_carryout), .out(result[6]));
  xor xor_8 (xor_8_out, B[7], sub);
  _1bitAdd u_1bitadd_8 (
    .b(xor_8_out), .a(A[7]), .carryin(n1bitadd_7_carryout), .carryout(n1bitadd_8_carryout), .out(result[7]));
  xor xor_9 (xor_9_out, B[8], sub);
  _1bitAdd u_1bitadd_9 (
    .b(xor_9_out), .a(A[8]), .carryin(n1bitadd_8_carryout), .carryout(n1bitadd_9_carryout), .out(result[8]));
  xor xor_10 (xor_10_out, B[9], sub);
  _1bitAdd u_1bitadd_10 (
    .b(xor_10_out), .a(A[9]), .carryin(n1bitadd_9_carryout), .carryout(n1bitadd_10_carryout), .out(result[9]));
  xor xor_11 (xor_11_out, B[10], sub);
  _1bitAdd u_1bitadd_11 (
    .b(xor_11_out), .a(A[10]), .carryin(n1bitadd_10_carryout), .carryout(n1bitadd_11_carryout),
    .out(result[10]));
  xor xor_12 (xor_12_out, B[11], sub);
  _1bitAdd u_1bitadd_12 (
    .b(xor_12_out), .a(A[11]), .carryin(n1bitadd_11_carryout), .carryout(n1bitadd_12_carryout),
    .out(result[11]));
  xor xor_13 (xor_13_out, B[12], sub);
  _1bitAdd u_1bitadd_13 (
    .b(xor_13_out), .a(A[12]), .carryin(n1bitadd_12_carryout), .carryout(n1bitadd_13_carryout),
    .out(result[12]));
  xor xor_14 (xor_14_out, B[13], sub);
  _1bitAdd u_1bitadd_14 (
    .b(xor_14_out), .a(A[13]), .carryin(n1bitadd_13_carryout), .carryout(n1bitadd_14_carryout),
    .out(result[13]));
  xor xor_15 (xor_15_out, B[14], sub);
  _1bitAdd u_1bitadd_15 (
    .b(xor_15_out), .a(A[14]), .carryin(n1bitadd_14_carryout), .carryout(n1bitadd_15_carryout),
    .out(result[14]));
  xor xor_16 (xor_16_out, B[15], sub);
  _1bitAdd u_1bitadd_16 (
    .b(xor_16_out), .a(A[15]), .carryin(n1bitadd_15_carryout), .carryout(n1bitadd_16_carryout),
    .out(result[15]));
  xor xor_17 (ovf, n1bitadd_16_carryout, n1bitadd_15_carryout);

  // Other names for the same wires on the sheet: a_t = A[0]; b_t = A[1]; c = A[2]; d = A[3]; e = A[4]; f = A[5];
  //   g = A[6]; h = A[7]; i = A[8]; j = A[9]; k = A[10]; l = A[11]; m = A[12]; n = A[13]; o = A[14]; p = A[15];
  //   _1 = B[0]; _2 = B[1]; _3 = B[2]; _4 = B[3]; _5 = B[4]; _6 = B[5]; _7 = B[6]; _8 = B[7]; _9 = B[8]; _10 = B[9];
  //   _11 = B[10]; _12 = B[11]; _13 = B[12]; _14 = B[13]; _15 = B[14]; _16 = B[15]
endmodule

module _3BitShiftL (
  input  [15:0] in_1,
  input  [2:0] in_2,
  output [15:0] out_3
);

  wire decoder_1_out1, decoder_1_out2, decoder_1_out3, decoder_1_out4, decoder_1_out5, decoder_1_out6,
       decoder_1_out7, or_1_out, or_2_out, or_3_out, or_4_out, or_5_out, or_6_out;
  wire [15:0] shiftleftone_1_out_3, shiftleftone_2_out_3, shiftleftone_3_out_3, shiftleftone_4_out_3,
       shiftleftone_5_out_3, shiftleftone_6_out_3;

  Decoder #(.select(3), .enable("false")) decoder_1 (
    .out1(decoder_1_out1), .out2(decoder_1_out2), .out3(decoder_1_out3), .out4(decoder_1_out4),
    .out5(decoder_1_out5), .out6(decoder_1_out6), .out7(decoder_1_out7), .sel(in_2));  // open: out0
  or or_1 (or_1_out, decoder_1_out6, decoder_1_out7);
  or or_2 (or_2_out, decoder_1_out4, or_3_out);
  or or_3 (or_3_out, decoder_1_out5, or_1_out);
  or or_4 (or_4_out, decoder_1_out3, or_2_out);
  or or_5 (or_5_out, decoder_1_out1, or_6_out);
  or or_6 (or_6_out, decoder_1_out2, or_4_out);
  shiftLeftOne shiftleftone_1 (.in_1(in_1), .ShftCntr(or_5_out), .out_3(shiftleftone_1_out_3));
  shiftLeftOne shiftleftone_2 (.in_1(shiftleftone_1_out_3), .ShftCntr(or_6_out), .out_3(shiftleftone_2_out_3));
  shiftLeftOne shiftleftone_3 (.in_1(shiftleftone_2_out_3), .ShftCntr(or_4_out), .out_3(shiftleftone_3_out_3));
  shiftLeftOne shiftleftone_4 (.in_1(shiftleftone_3_out_3), .ShftCntr(or_2_out), .out_3(shiftleftone_4_out_3));
  shiftLeftOne shiftleftone_5 (.in_1(shiftleftone_4_out_3), .ShftCntr(or_3_out), .out_3(shiftleftone_5_out_3));
  shiftLeftOne shiftleftone_6 (.in_1(shiftleftone_5_out_3), .ShftCntr(or_1_out), .out_3(shiftleftone_6_out_3));
  shiftLeftOne shiftleftone_7 (.in_1(shiftleftone_6_out_3), .ShftCntr(decoder_1_out7), .out_3(out_3));
endmodule

module _3BitShiftR (
  input  [15:0] in_1,
  input  [2:0] in_2,
  output [15:0] out_3
);

  wire decoder_1_out1, decoder_1_out2, decoder_1_out3, decoder_1_out4, decoder_1_out5, decoder_1_out6,
       decoder_1_out7, or_1_out, or_2_out, or_3_out, or_4_out, or_5_out, or_6_out;
  wire [15:0] shiftrightone_1_out_3, shiftrightone_2_out_3, shiftrightone_3_out_3, shiftrightone_4_out_3,
       shiftrightone_5_out_3, shiftrightone_6_out_3;

  Decoder #(.select(3), .enable("false")) decoder_1 (
    .out1(decoder_1_out1), .out2(decoder_1_out2), .out3(decoder_1_out3), .out4(decoder_1_out4),
    .out5(decoder_1_out5), .out6(decoder_1_out6), .out7(decoder_1_out7), .sel(in_2));  // open: out0
  or or_1 (or_1_out, decoder_1_out6, decoder_1_out7);
  or or_2 (or_2_out, decoder_1_out4, or_3_out);
  or or_3 (or_3_out, decoder_1_out5, or_1_out);
  or or_4 (or_4_out, decoder_1_out3, or_2_out);
  or or_5 (or_5_out, decoder_1_out1, or_6_out);
  or or_6 (or_6_out, decoder_1_out2, or_4_out);
  shiftRightOne shiftrightone_1 (.in_1(in_1), .ShftCntr(or_5_out), .out_3(shiftrightone_1_out_3));
  shiftRightOne shiftrightone_2 (.in_1(shiftrightone_1_out_3), .ShftCntr(or_6_out), .out_3(shiftrightone_2_out_3));
  shiftRightOne shiftrightone_3 (.in_1(shiftrightone_2_out_3), .ShftCntr(or_4_out), .out_3(shiftrightone_3_out_3));
  shiftRightOne shiftrightone_4 (.in_1(shiftrightone_3_out_3), .ShftCntr(or_2_out), .out_3(shiftrightone_4_out_3));
  shiftRightOne shiftrightone_5 (.in_1(shiftrightone_4_out_3), .ShftCntr(or_3_out), .out_3(shiftrightone_5_out_3));
  shiftRightOne shiftrightone_6 (.in_1(shiftrightone_5_out_3), .ShftCntr(or_1_out), .out_3(shiftrightone_6_out_3));
  shiftRightOne shiftrightone_7 (.in_1(shiftrightone_6_out_3), .ShftCntr(decoder_1_out7), .out_3(out_3));
endmodule

module _1bitAdd (
  input  carryin,
  input  b,
  input  a,
  output out,
  output carryout
);

  wire and_1_out, and_2_out, xor_1_out;

  and and_1 (and_1_out, b, a);
  or or_1 (carryout, and_1_out, and_2_out);
  xor xor_1 (xor_1_out, b, a);
  and and_2 (and_2_out, xor_1_out, carryin);
  xor xor_2 (out, xor_1_out, carryin);
endmodule

module shiftRightOne (
  input  [15:0] in_1,
  input  ShftCntr,
  output [15:0] out_3
);

  Multiplexer #(.enable("false")) multiplexer_1 (.in0(in_1[0]), .in1(in_1[1]), .out(out_3[0]), .sel(ShftCntr));
  Multiplexer #(.enable("false")) multiplexer_2 (.in0(in_1[1]), .in1(in_1[2]), .out(out_3[1]), .sel(ShftCntr));
  Multiplexer #(.enable("false")) multiplexer_3 (.in0(in_1[2]), .in1(in_1[3]), .out(out_3[2]), .sel(ShftCntr));
  Multiplexer #(.enable("false")) multiplexer_4 (.in0(in_1[3]), .in1(in_1[4]), .out(out_3[3]), .sel(ShftCntr));
  Multiplexer #(.enable("false")) multiplexer_5 (.in0(in_1[4]), .in1(in_1[5]), .out(out_3[4]), .sel(ShftCntr));
  Multiplexer #(.enable("false")) multiplexer_6 (.in0(in_1[5]), .in1(in_1[6]), .out(out_3[5]), .sel(ShftCntr));
  Multiplexer #(.enable("false")) multiplexer_7 (.in0(in_1[6]), .in1(in_1[7]), .out(out_3[6]), .sel(ShftCntr));
  Multiplexer #(.enable("false")) multiplexer_8 (.in0(in_1[7]), .in1(in_1[8]), .out(out_3[7]), .sel(ShftCntr));
  Multiplexer #(.enable("false")) multiplexer_9 (.in0(in_1[8]), .in1(in_1[9]), .out(out_3[8]), .sel(ShftCntr));
  Multiplexer #(.enable("false")) multiplexer_10 (.in0(in_1[9]), .in1(in_1[10]), .out(out_3[9]), .sel(ShftCntr));
  Multiplexer #(.enable("false")) multiplexer_11 (.in0(in_1[10]), .in1(in_1[11]), .out(out_3[10]), .sel(ShftCntr));
  Multiplexer #(.enable("false")) multiplexer_12 (.in0(in_1[11]), .in1(in_1[12]), .out(out_3[11]), .sel(ShftCntr));
  Multiplexer #(.enable("false")) multiplexer_13 (.in0(in_1[12]), .in1(in_1[13]), .out(out_3[12]), .sel(ShftCntr));
  Multiplexer #(.enable("false")) multiplexer_14 (.in0(in_1[13]), .in1(in_1[14]), .out(out_3[13]), .sel(ShftCntr));
  Multiplexer #(.enable("false")) multiplexer_15 (.in0(in_1[14]), .in1(in_1[15]), .out(out_3[14]), .sel(ShftCntr));
  Multiplexer #(.enable("false")) multiplexer_16 (.in0(in_1[15]), .in1(in_1[15]), .out(out_3[15]), .sel(ShftCntr));
endmodule

module shiftLeftOne (
  input  [15:0] in_1,
  input  ShftCntr,
  output [15:0] out_3
);

  Multiplexer #(.enable("false")) multiplexer_1 (.in0(in_1[15]), .in1(in_1[14]), .out(out_3[15]), .sel(ShftCntr));
  Multiplexer #(.enable("false")) multiplexer_2 (.in0(in_1[14]), .in1(in_1[13]), .out(out_3[14]), .sel(ShftCntr));
  Multiplexer #(.enable("false")) multiplexer_3 (.in0(in_1[13]), .in1(in_1[12]), .out(out_3[13]), .sel(ShftCntr));
  Multiplexer #(.enable("false")) multiplexer_4 (.in0(in_1[12]), .in1(in_1[11]), .out(out_3[12]), .sel(ShftCntr));
  Multiplexer #(.enable("false")) multiplexer_5 (.in0(in_1[11]), .in1(in_1[10]), .out(out_3[11]), .sel(ShftCntr));
  Multiplexer #(.enable("false")) multiplexer_6 (.in0(in_1[10]), .in1(in_1[9]), .out(out_3[10]), .sel(ShftCntr));
  Multiplexer #(.enable("false")) multiplexer_7 (.in0(in_1[9]), .in1(in_1[8]), .out(out_3[9]), .sel(ShftCntr));
  Multiplexer #(.enable("false")) multiplexer_8 (.in0(in_1[8]), .in1(in_1[7]), .out(out_3[8]), .sel(ShftCntr));
  Multiplexer #(.enable("false")) multiplexer_9 (.in0(in_1[7]), .in1(in_1[6]), .out(out_3[7]), .sel(ShftCntr));
  Multiplexer #(.enable("false")) multiplexer_10 (.in0(in_1[6]), .in1(in_1[5]), .out(out_3[6]), .sel(ShftCntr));
  Multiplexer #(.enable("false")) multiplexer_11 (.in0(in_1[5]), .in1(in_1[4]), .out(out_3[5]), .sel(ShftCntr));
  Multiplexer #(.enable("false")) multiplexer_12 (.in0(in_1[4]), .in1(in_1[3]), .out(out_3[4]), .sel(ShftCntr));
  Multiplexer #(.enable("false")) multiplexer_13 (.in0(in_1[3]), .in1(in_1[2]), .out(out_3[3]), .sel(ShftCntr));
  Multiplexer #(.enable("false")) multiplexer_14 (.in0(in_1[2]), .in1(in_1[1]), .out(out_3[2]), .sel(ShftCntr));
  Multiplexer #(.enable("false")) multiplexer_15 (.in0(in_1[1]), .in1(in_1[0]), .out(out_3[1]), .sel(ShftCntr));
  Multiplexer #(.enable("false")) multiplexer_16 (.in0(in_1[0]), .in1(1'b0), .out(out_3[0]), .sel(ShftCntr));
endmodule
